# Fritzing sketch Photobooth (saved by Fritzing 0.9.3b)
breadboards: 1

parts:
  Raspberry_Pi_1 = Raspberry Pi 3 [part_number=RPI-3-V1.2]
  S1 = Round Pushbutton
  S2 = Round Pushbutton

nets:
  N1: Raspberry_Pi_1.3v3, S1.leg1, S2.leg1
  N2: Raspberry_Pi_1.GIPO17, S2.leg0
  N3: Raspberry_Pi_1.GIPO18, S1.leg0

notes:
  Blanc = Flash = GPIO 4
  Vert = Bouton vert = GPIO 18
  Rouge = Bouton rouge = GPIO 17
  Bleu = ioniseur = GPIO 27
  Rose = ventilo = GPIO 22
